# Fritzing sketch MoistureServoArduinoUno12V (saved by Fritzing 0.9.2b)

parts:
  SoilMoisture = SparkFun Soil Moisture Sensor [part_number=SEN-13322]
  ArduinoUnoExt = Arduino Uno (Rev3)
  BarrelJack12v = Power plug
  Servo = Basic Servo

nets:
  VCC: SoilMoisture.VCC, ArduinoUnoExt.5V, Servo.vcc
  GND: SoilMoisture.GND, ArduinoUnoExt.GND, BarrelJack12v.GND, Servo.gnd
  N1: SoilMoisture.SIG, ArduinoUnoExt.A2
  N2: ArduinoUnoExt.D10_PWM/SS, Servo.pulse
  VIN: ArduinoUnoExt.VIN, BarrelJack12v.VCC

custom parts:
  SparkFun Soil Moisture Sensor: The SparkFun Soil Moisture Sensor is a simple breakout for measuring the moisture in soil and similar materials.
